# Fritzing sketch ModuloToque (saved by Fritzing 1.0.6)
breadboards: 1

parts:
  A1 = Esp32-c3 super mini
  LED1 = LED - 5mm [color="Red (633nm)" current=0.030A package="5 mm [THT]"]
  R1 = Resistor [tolerance=±5% power=0.25W resistance=330 package=THT]
  TTP223B2 = TTP223B Capacitive Touch Sensor Module [part_number="Touch sensor"]
  TTP223B3 = TTP223B Capacitive Touch Sensor Module [part_number="Touch sensor"]

nets:
  N1: A1.Pin_5, R1.Pin_0
  N2: A1.Pin_7, TTP223B3.SIG
  N3: A1.Pin_10, TTP223B2.SIG
  GND: A1.Pin_15, LED1.cathode, TTP223B2.GND, TTP223B3.GND
  VCC: A1.Pin_16, TTP223B2.VCC, TTP223B3.VCC
  N4: LED1.anode, R1.Pin_1

custom parts:
  Esp32-c3 super mini: ESP32-C3 Development Board ESP32 SuperMini Development Board ESP32 Development Board WiFi Bluetooth.
  TTP223B Capacitive Touch Sensor Module: The TTP223B capacitive touch sensor module uses the TTP223B IC. The appropriate voltage is approximately 2 to 5.5 volts.
