# Fritzing sketch NFCBuzzerProject (saved by Fritzing 1.0.6)
breadboards: 1

parts:
  A1 = Esp32-c3 super mini
  Componente1 = PN532 Elechouse RFID NFC Module V3
  J1 = Piezo Speaker

nets:
  N1: A1.Pin_4, J1.pin2
  N2: A1.Pin_8, Componente1.SDA
  N3: A1.Pin_9, Componente1.SCL
  N4: A1.Pin_14, Componente1.GND, J1.pin1
  N5: A1.Pin_15, Componente1.VCC

custom parts:
  Esp32-c3 super mini: ESP32-C3 Development Board ESP32 SuperMini Development Board ESP32 Development Board WiFi Bluetooth.
  PN532 Elechouse RFID NFC Module V3: NFC is a popular technology in recent years. We often heard this work while smart phone company such as Samsung or HTC introduces their latest high-end phones. Almost all the high-end phone in the market support NFC. Near field communication (NFC) is a set of standards for smart phones and similar devices to establish radio communication with each other by touching them together or bringing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
